# Fritzing sketch wk11_led (saved by Fritzing 0.9.3b)

parts:
  元件1 = Arduino Uno (Rev3)
  LED1 = LED - 5mm [color="Red (633nm)" package="5 mm [THT]"]
  LED2 = LED - 5mm [color="Red (633nm)" package="5 mm [THT]"]

nets:
  N1: 元件1.D12/MISO, LED2.anode
  N2: 元件1.D13/SCK, LED1.anode
  N3: 元件1.GND, LED1.cathode, LED2.cathode
